# Fritzing sketch Earthquake-Warning-System (saved by Fritzing 0.9.6b)

parts:
  Part1 = InvenSense MPU6050
  U1 = NodeMCU V1.0
  U2 = LM2596 step down module
  TP1 = TP4056 [chip_label=TP4056 package="DIP (Dual Inline) [THT]"]
  Squix1 = OLED 0.96" 128x64 I2C SSD1306
  BATT1 = LiPoly Battery (1300mAh)
  SPKR1 = Loudspeaker
  SPKR2 = Loudspeaker
  SPKR3 = Loudspeaker  # not connected
  AMP1 = PAM8403 6W Stereo Amplifier
  Tiny_RTC1 = Tiny RTC
  S3 = Toggle Switch [package=THT]
  S6 = Pushbutton [package="[THT]"]
  S4 = Pushbutton [package="[THT]"]
  S5 = Pushbutton [package="[THT]"]
  S7 = Pushbutton [package="[THT]"]
  S8 = Pushbutton [package=THT]
  S9 = SWITCH-MOMENTARY-2 [package=tactile-pth-12mm]
  S10 = Round Pushbutton
  SW-1 = Vibration sensor module

nets:
  VCC: Part1.VCC, U1.3V3, Squix1.VCC, Tiny_RTC1.VCC, SW-1.vcc
  GND: Part1.GND, U1.GND, U2.IN-, U2.OUT-, TP1.pin6, AMP1.POWER-, AMP1.INPUTG, Tiny_RTC1.GND, S8.leg0, S9.2, SW-1.Ground
  N1: Part1.SCL, U1.D1, Squix1.SCL, Tiny_RTC1.SCL
  N2: Part1.SDA, U1.D2, Squix1.SCA, Tiny_RTC1.SDA
  N3: U1.D0, SW-1.Digital_output
  N4: U1.D3, AMP1.INPUTL, AMP1.INPUTR
  N5: U1.D6, S7.Pin_3
  N6: U1.D7, S6.Pin_3
  N7: U1.D8, S5.Pin_3
  N8: U1.RX, S4.Pin_3
  N9: U1.Vin, U2.IN+, S10.leg0
  N10: U1.RST, S9.1
  N11: U2.OUT+, AMP1.POWER+
  N12: TP1.pin3, S3.L1
  N13: TP1.pin4, BATT1.positive, S3.L2
  N14: TP1.pin5, BATT1.negative
  N15: Squix1.GND, S6.Pin_1, S6.Pin_2, S4.Pin_1, S4.Pin_2, S5.Pin_1, S5.Pin_2, S7.Pin_1, S7.Pin_2, S8.leg1
  N16: SPKR1.pin1, SPKR2.pin1, AMP1.ROUT-, AMP1.LOUT-
  N17: SPKR1.pin2, SPKR2.pin2, AMP1.ROUT+, AMP1.LOUT+
  N18: S3.COM, S10.leg1

custom parts:
  NodeMCU V1.0: ESP8266 based NodeMCU
  LM2596 step down module: LM2596 DC-DC step down power supply module 3 A.
  TP4056: A DIP stand-in part for whatever IC you want. With 6 pins on a 300mil dual inline package (DIP) footprint.
  LiPoly Battery (1300mAh): Lithium Ion Polymer Battery (1300mAh)
  PAM8403 6W Stereo Amplifier: PAM8403 6 Watt Stereo Amplifier
  Tiny RTC: Tiny RTC I2C module DS1370Z RTC and AT24C32 EEPROM
  Vibration sensor module: Single-roller type full induction trigger switch. When no vibration or tilt, the product is ON conduction state, and in the steady state, when a vibration or tilt, the switch will be rendered instantly disconnect the conductive resistance increases, generating a current pulse signal, thereby triggering circuit. The default state of the swith is close Digital output Supply voltage:3.3V-5V On-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
